// Logisim project micro.circ as structural Verilog: 1 circuit, main circuit EV20_Superescalar
module EV20_Superescalar (
  input  in_1
);

  wire and_1_out, bloque1_1_preload, CLK, CLK2, CLK3, CLK4, dipswitch_1_sw1, dipswitch_2_sw1, HOLD,
       memory_unit_control_1_is_free, New_data_arrive, not_1_out, not_2_out, not_3_out, register_1_q,
       uc1_1_aluenable, uc1_1_loadstoreenable, undriven, undriven_2, undriven_3, undriven_5;
  wire [1:0] ALU_Pipeline_sh_out, LoadStore_mrymw_out, LoadStore_sh_out, MREtapa2Pipeline, Mux_select,
       pipeline_register_1_mrymw_out, pipeline_register_1_sh_out, pipeline_register_2_mrymw_out,
       pipeline_register_2_sh_out, undriven_4;
  wire [3:0] ALU_Pipeline_aluc_out, LoadStore_aluc_out, pipeline_register_1_aluc_out,
       pipeline_register_2_aluc_out;
  wire [5:0] A_Etapa1, ALU_Pipeline_a_bus_out, ALU_Pipeline_b_bus_out, ALU_Pipeline_c_bus_out,
       ALU_Pipeline_t_bus_out, B_Etapa1, C_Etapa1, C_Etapa2Alu, C_Etapa3, judge_1_a_bus, judge_1_b_bus,
       LoadStore_a_bus_out, LoadStore_b_bus_out, LoadStore_c_bus_out, LoadStore_t_bus_out,
       pipeline_register_1_t_bus_out, pipeline_register_2_t_bus_out, reg_C_address, register_bank_1_p6,
       register_bank_1_p7;
  wire [8:8] ALU_Pipeline_kmx_out, LoadStore_kmx_out, pipeline_register_1_kmx_out,
       pipeline_register_2_kmx_out;
  wire [9:0] ALU_Pipeline_d_address_out, instruction2register_1_daddresss, LoadStore_d_address_out,
       pipeline_register_1_d_address_out, register_2_q;
  wire [10:0] ProgramCounterReg_pc;
  wire [14:0] judge_1_reg_out, MicroInstructionROM_microinstruction;
  wire [15:0] ALU_RESULT, ALUALULAU_z, BusA_ALU_q, BusA_LS_q, BusB_ALU_q, Constant_K_q, data_1_datamemout,
       instruction2register_1_k, multiplexer_1_out, reg_A_read, reg_B_read, reg_C_write, register_4_q;
  wire [23:0] BBUS, ProgramMemory_data;

  // Probe on ProgramCounterReg_pc
  DipSwitch #(.number(2)) dipswitch_1 (.sw1(dipswitch_1_sw1));  // open: sw2
  ROM #(.addrWidth(11), .dataWidth(24)) ProgramMemory (.addr(ProgramCounterReg_pc), .data(ProgramMemory_data));
  // Probe on undriven
  // Probe on undriven_2
  // Probe on undriven_3
  // Probe on undriven_4[1]
  // Probe on undriven_4[0]
  // Probe on undriven_5
  Bloque1 bloque1_1 (.Preload(bloque1_1_preload), .jump_type(BBUS[21:20]), .register_to_test(16'hfff));  // open: CY
  ClockGenerator clocks (.Auto(dipswitch_1_sw1), .ManualCLK(in_1), .CLK(CLK), .CLK2(CLK2), .CLK3(CLK3), .CLK4(CLK4));
  and and_1 (and_1_out, BBUS[22], bloque1_1_preload);
  Register #(.width(24)) InstructionRegister (.D(ProgramMemory_data), .en(1'b1), .clk(CLK), .Q(BBUS));  // open: clr
  PCreg ProgramCounterReg (
    .PC(ProgramCounterReg_pc), .HOLD(1'b0), .Preload(and_1_out), .CLK1(CLK),
    .displacement_or_address(BBUS[15:5]));
  // Probe on BBUS
  // Probe on reg_A_read
  // Probe on reg_B_read
  instruction2register instruction2register_1 (
    .Instruction(BBUS), .Daddresss(instruction2register_1_daddresss), .A(A_Etapa1), .B(B_Etapa1),
    .C(C_Etapa1), .K(instruction2register_1_k));
  Micro_Instruction_ROM MicroInstructionROM (
    .Instruction(BBUS), .MicroInstruction(MicroInstructionROM_microinstruction));
  // register_bank register_bank_1: pin names not known; wires that end beside it: reg_A_read, CLK, reg_B_read, reg_C_write, reg_C_address, register_bank_1_p6, register_bank_1_p7
  // Probe on MicroInstructionROM_microinstruction[14:11]
  // Probe on MicroInstructionROM_microinstruction[10:9]
  // Probe on MicroInstructionROM_microinstruction[8]
  // Probe on MicroInstructionROM_microinstruction[7]
  // Probe on MicroInstructionROM_microinstruction[6]
  // Probe on MicroInstructionROM_microinstruction[5:0]
  Register #(.width(16), .trigger("falling")) Constant_K (
    .D(instruction2register_1_k), .clk(CLK2), .Q(Constant_K_q));  // open: en, clr
  // Probe on register_bank_1_p7
  Pipeline_register pipeline_register_1 (
    .ALUC_OUT(pipeline_register_1_aluc_out), .B_bus_IN(B_Etapa1),
    .SH_IN(MicroInstructionROM_microinstruction[10:9]), .D_Address_OUT(pipeline_register_1_d_address_out),
    .C_bus_OUT(C_Etapa2Alu), .A_bus_OUT(register_bank_1_p6),
    .ALUC_IN(MicroInstructionROM_microinstruction[14:11]), .A_bus_IN(A_Etapa1),
    .D_Address_IN(instruction2register_1_daddresss), .MRyMW_OUT(pipeline_register_1_mrymw_out),
    .SH_OUT(pipeline_register_1_sh_out), .C_bus_IN(C_Etapa1),
    .Kmx_IN(MicroInstructionROM_microinstruction[8]), .B_bus_OUT(register_bank_1_p7),
    .T_bus_OUT(pipeline_register_1_t_bus_out), .CLK(CLK2),
    .MRyMW_IN(MicroInstructionROM_microinstruction[7:6]),
    .T_bus_IN(MicroInstructionROM_microinstruction[5:0]), .Kmx_OUT(pipeline_register_1_kmx_out[8]));  // open: Hold
  Multiplexer #(.width(16), .enable("false")) multiplexer_1 (
    .in0(reg_A_read), .in1(Constant_K_q), .out(multiplexer_1_out), .sel(pipeline_register_1_kmx_out[8]));
  Register #(.width(16)) BusA_ALU (
    .D(multiplexer_1_out), .en(uc1_1_aluenable), .clk(CLK2), .Q(BusA_ALU_q));  // open: clr
  // Probe on register_bank_1_p6
  // Probe on pipeline_register_1_aluc_out
  // Probe on pipeline_register_1_sh_out
  // Probe on pipeline_register_1_kmx_out[8]
  // Probe on pipeline_register_1_mrymw_out[1]
  // Probe on pipeline_register_1_mrymw_out[0]
  // Probe on pipeline_register_1_t_bus_out
  Register #(.width(16)) BusB_ALU (.D(reg_B_read), .en(uc1_1_aluenable), .clk(CLK2), .Q(BusB_ALU_q));  // open: clr
  // Probe on BusA_ALU_q
  // Probe on BusB_ALU_q
  UC1 uc1_1 (
    .HOLD(HOLD), .MRyMW_OUT_E1(pipeline_register_1_mrymw_out), .ALUisFree(1'b1), .MEMisFree(1'b1),
    .ALUEnable(uc1_1_aluenable), .LoadStoreEnable(uc1_1_loadstoreenable));
  ALU ALUALULAU (.ALUC(ALU_Pipeline_aluc_out), .A(BusA_ALU_q), .B(BusB_ALU_q), .Z(ALUALULAU_z));  // open: CYin, CYout
  // Probe on ALUALULAU_z
  Register #(.width(1)) register_1 (.D(uc1_1_loadstoreenable), .clk(CLK2), .Q(register_1_q));  // open: en, clr
  not not_1 (not_1_out, CLK3);
  and and_2 (New_data_arrive, register_1_q, not_1_out);
  not not_2 (not_2_out, uc1_1_aluenable);
  not not_3 (not_3_out, uc1_1_loadstoreenable);
  Register #(.width(10)) register_2 (
    .D(LoadStore_d_address_out), .en(uc1_1_loadstoreenable), .clk(CLK2), .Q(register_2_q));  // open: clr
  Register #(.width(16)) BusA_LS (.D(reg_A_read), .en(uc1_1_loadstoreenable), .clk(CLK2), .Q(BusA_LS_q));  // open: clr
  Register #(.width(16)) register_3 (.D(ALUALULAU_z), .en(1'b1), .clk(CLK2), .Q(ALU_RESULT));  // open: clr
  Pipeline_register ALU_Pipeline (
    .ALUC_OUT(ALU_Pipeline_aluc_out), .B_bus_IN(register_bank_1_p7), .SH_IN(pipeline_register_1_sh_out),
    .D_Address_OUT(ALU_Pipeline_d_address_out), .C_bus_OUT(ALU_Pipeline_c_bus_out),
    .A_bus_OUT(ALU_Pipeline_a_bus_out), .ALUC_IN(pipeline_register_1_aluc_out),
    .A_bus_IN(register_bank_1_p6), .D_Address_IN(pipeline_register_1_d_address_out),
    .MRyMW_OUT(MREtapa2Pipeline), .SH_OUT(ALU_Pipeline_sh_out), .C_bus_IN(C_Etapa2Alu),
    .Kmx_IN(pipeline_register_1_kmx_out[8]), .Hold(not_2_out), .B_bus_OUT(ALU_Pipeline_b_bus_out),
    .T_bus_OUT(ALU_Pipeline_t_bus_out), .CLK(CLK3), .MRyMW_IN(pipeline_register_1_mrymw_out),
    .T_bus_IN(pipeline_register_1_t_bus_out), .Kmx_OUT(ALU_Pipeline_kmx_out[8]));
  Pipeline_register LoadStore (
    .ALUC_OUT(LoadStore_aluc_out), .B_bus_IN(register_bank_1_p7), .SH_IN(pipeline_register_1_sh_out),
    .D_Address_OUT(LoadStore_d_address_out), .C_bus_OUT(LoadStore_c_bus_out),
    .A_bus_OUT(LoadStore_a_bus_out), .ALUC_IN(pipeline_register_1_aluc_out), .A_bus_IN(register_bank_1_p6),
    .D_Address_IN(pipeline_register_1_d_address_out), .MRyMW_OUT(LoadStore_mrymw_out),
    .SH_OUT(LoadStore_sh_out), .C_bus_IN(C_Etapa2Alu), .Kmx_IN(pipeline_register_1_kmx_out[8]),
    .Hold(not_3_out), .B_bus_OUT(LoadStore_b_bus_out), .T_bus_OUT(LoadStore_t_bus_out), .CLK(CLK3),
    .MRyMW_IN(pipeline_register_1_mrymw_out), .T_bus_IN(pipeline_register_1_t_bus_out),
    .Kmx_OUT(LoadStore_kmx_out[8]));
  Data data_1 (
    .DAddress(register_2_q), .clk(CLK2), .Enable(register_1_q), .DataMemInput(BusA_LS_q),
    .DataMemOut(data_1_datamemout));  // open: M
  // Probe on ALU_Pipeline_aluc_out
  // Probe on ALU_Pipeline_sh_out
  // Probe on ALU_Pipeline_kmx_out[8]
  // Probe on MREtapa2Pipeline[1]
  // Probe on MREtapa2Pipeline[0]
  // Probe on ALU_Pipeline_t_bus_out
  // Probe on ALU_Pipeline_c_bus_out
  // Probe on LoadStore_aluc_out
  // Probe on LoadStore_sh_out
  // Probe on LoadStore_kmx_out[8]
  // Probe on LoadStore_mrymw_out[1]
  // Probe on LoadStore_mrymw_out[0]
  // Probe on LoadStore_t_bus_out
  // Probe on LoadStore_d_address_out
  // Probe on memory_unit_control_1_is_free
  memory_unit_control memory_unit_control_1 (
    .set_free(dipswitch_2_sw1), .set_not_free(New_data_arrive), .clk(CLK2),
    .is_free(memory_unit_control_1_is_free), .is_done(Mux_select[1]));
  DipSwitch #(.number(2)) dipswitch_2 (.sw1(dipswitch_2_sw1), .sw2(Mux_select[0]));
  Register #(.width(16)) register_4 (.D(data_1_datamemout), .en(1'b1), .clk(CLK2), .Q(register_4_q));  // open: clr
  Multiplexer #(.width(16), .enable("false")) multiplexer_2 (
    .in0(ALU_RESULT), .in1(register_4_q), .out(reg_C_write), .sel(Mux_select[1]));
  // UC2 uc2_1: pin names not known; wires that end beside it: A_Etapa1, B_Etapa1, C_Etapa1, C_Etapa2Alu, C_Etapa2Alu, C_Etapa3, CLK, CLK, HOLD
  judge judge_1 (
    .reg_in_alu({ALU_Pipeline_aluc_out, ALU_Pipeline_sh_out, ALU_Pipeline_kmx_out[8], MREtapa2Pipeline, ALU_Pipeline_t_bus_out}),
    .reg_in_memory({LoadStore_aluc_out, LoadStore_sh_out, LoadStore_kmx_out[8], LoadStore_mrymw_out, LoadStore_t_bus_out}),
    .A_alu(ALU_Pipeline_a_bus_out), .A_mem(LoadStore_a_bus_out), .B_alu(ALU_Pipeline_b_bus_out),
    .B_mem(LoadStore_b_bus_out), .C_alu(ALU_Pipeline_c_bus_out), .C_mem(LoadStore_c_bus_out),
    .in_9(Mux_select), .reg_out(judge_1_reg_out), .A_bus(judge_1_a_bus), .B_bus(judge_1_b_bus),
    .C_bus(C_Etapa3));
  Pipeline_register pipeline_register_2 (
    .ALUC_OUT(pipeline_register_2_aluc_out), .B_bus_IN(judge_1_b_bus), .SH_IN(judge_1_reg_out[10:9]),
    .C_bus_OUT(reg_C_address), .ALUC_IN(judge_1_reg_out[14:11]), .A_bus_IN(judge_1_a_bus),
    .MRyMW_OUT(pipeline_register_2_mrymw_out), .SH_OUT(pipeline_register_2_sh_out), .C_bus_IN(C_Etapa3),
    .Kmx_IN(judge_1_reg_out[8]), .Hold(HOLD), .T_bus_OUT(pipeline_register_2_t_bus_out), .CLK(CLK3),
    .MRyMW_IN(judge_1_reg_out[7:6]), .T_bus_IN(judge_1_reg_out[5:0]), .Kmx_OUT(pipeline_register_2_kmx_out[8]));  // open: D_Address_OUT, A_bus_OUT, D_Address_IN, B_bus_OUT

  // Other names for the same wires on the sheet: C_Etapa2Mem[5:0] = C_Etapa2Alu; pulseGenManual = in_1

  // Notes on the sheet:
  //   contents of ProgramMemory (hex, n*v repeats v):
  //   200001
  //   splitters que encajar con los registros de pipeline
  //   para hacer copy-paste
  //   probes que encajar en los splitters de arriba
  //   INSTRUCTION
  //   REGISTER
  //   //todo: condensar los selectores en un solo bloque
  //   Detecto nueva operacion de memoria
  //   El mux es el de los is_done , el menos significativo es el de la ALU que se pone en 1 cuando termino
endmodule
